# Fritzing sketch alu-1st-floor-v2 (saved by Fritzing 0.9.1b)
circuit board: 9.99cm x 9.98483cm
breadboards: 1

parts:
  OUTPUT_B2 = female pin header, 8 pins [form="♀ (female)"]
  OUTPUT_A2 = female pin header, 8 pins [form="♀ (female)"]
  J6 = female pin header, 2 pins [form="♀ (female)"]
  J7 = female pin header, 8 pins [form="♀ (female)"]
  J8 = female pin header, 8 pins [form="♀ (female)"]
  J9 = female pin header, 2 pins [form="♀ (female)"]
  74LS283-1 = IC, DIP package, 16 pins [chip_label=IC]
  74LS283-2 = IC, DIP package, 16 pins [chip_label=IC]
  74LS157-1 = IC, DIP package, 16 pins [chip_label=IC]
  74LS157-2 = IC, DIP package, 16 pins [chip_label=IC]
  C1 = Ceramic Capacitor [capacitance=100nF package="100 mil [THT, multilayer]"]
  J10 = female pin header, 5 pins [form="♀ (female)"]
  J11 = female pin header, 4 pins [form="♀ (female)"]

nets:
  N1: OUTPUT_B2.pin1, J8.pin1, 74LS283-1.pin11
  N2: OUTPUT_B2.pin2, J8.pin2, 74LS283-1.pin15
  N3: OUTPUT_B2.pin3, J8.pin3, 74LS283-1.pin2
  N4: OUTPUT_B2.pin4, J8.pin4, 74LS283-1.pin6
  N5: OUTPUT_B2.pin5, J8.pin5, 74LS283-2.pin11
  N6: OUTPUT_B2.pin6, J8.pin6, 74LS283-2.pin15
  N7: OUTPUT_B2.pin7, J8.pin7, 74LS283-2.pin2
  N8: OUTPUT_B2.pin8, J8.pin8, 74LS283-2.pin6
  N9: OUTPUT_A2.pin1, J7.pin1, 74LS283-1.pin12
  N10: OUTPUT_A2.pin2, J7.pin2, 74LS283-1.pin14
  N11: OUTPUT_A2.pin3, J7.pin3, 74LS283-1.pin3
  N12: OUTPUT_A2.pin4, J7.pin4, 74LS283-1.pin5
  N13: OUTPUT_A2.pin5, J7.pin5, 74LS283-2.pin12
  N14: OUTPUT_A2.pin6, J7.pin6, 74LS283-2.pin14
  N15: OUTPUT_A2.pin7, J7.pin7, 74LS283-2.pin3
  N16: OUTPUT_A2.pin8, J7.pin8, 74LS283-2.pin5
  N17: J6.pin1, J9.pin2
  N18: J6.pin2, J9.pin1
  N19: 74LS283-1.pin1, 74LS157-1.pin14, J10.pin4
  N20: 74LS283-1.pin4, 74LS157-1.pin11, J10.pin5
  N21: 74LS283-1.pin7, 74LS283-2.pin9
  N22: 74LS283-1.pin8, 74LS283-2.pin8, 74LS157-2.pin8, C1.0
  N23: 74LS283-1.pin9, J10.pin1
  N24: 74LS283-1.pin10, 74LS157-1.pin2, J10.pin2
  N25: 74LS283-1.pin13, 74LS157-1.pin5, J10.pin3
  N26: 74LS283-1.pin16, 74LS283-2.pin16, C1.1
  N27: 74LS283-2.pin1, 74LS157-2.pin14, J11.pin3
  N28: 74LS283-2.pin4, 74LS157-2.pin11, J11.pin4
  N29: 74LS283-2.pin10, 74LS157-2.pin2, J11.pin1
  N30: 74LS283-2.pin13, 74LS157-2.pin5, J11.pin2
