# Fritzing sketch crystalclock (saved by Fritzing 0.9.1b)
circuit board: 12.2564cm x 5.49691cm
breadboards: 1

parts:
  XTAL = female pin header, 1 pin [form="♀ (female)"]  # not connected
  RESET = female pin header, 1 pin [form="♀ (female)"]  # not connected
  J6 = female pin header, 4 pins [form="♀ (female)"]
  J7 = female pin header, 4 pins [form="♀ (female)"]
  OUTPUT = female pin header, 1 pin [form="♀ (female)"]  # not connected
  74LS169 = IC, DIP package, 16 pins [chip_label=IC]
  C1 = Ceramic Capacitor [capacitance=100nF package="100 mil [THT, multilayer]"]
  74LS14 = IC, DIP package, 14 pins [chip_label=IC]
  C2 = Ceramic Capacitor [capacitance=100nF package="100 mil [THT, multilayer]"]
  C4 = Ceramic Capacitor [capacitance=100nF package="100 mil [THT, multilayer]"]
  RE1 = Rotary Encoder [package=THT]
  J8 = female pin header, 1 pin [form="♀ (female)"]  # not connected
  J9 = female pin header, 1 pin [form="♀ (female)"]  # not connected
  C5 = Ceramic Capacitor [capacitance=100nF package="100 mil [THT, multilayer]"]
  R1 = Resistor [tolerance=±5% resistance=14k package=THT]
  R2 = Resistor [tolerance=±5% resistance=14k package=THT]
  MC14495 = IC, DIP package, 16 pins [chip_label=IC]
  5161AS = 7 Segment Display

nets:
  N1: J6.pin1, J6.pin2, 74LS169.pin3, 74LS169.pin4, 74LS169.pin5, 74LS169.pin6, 74LS169.pin7, 74LS169.pin8, 74LS169.pin10, C1.1, 74LS14.pin1, 74LS14.pin3, 74LS14.pin5, 74LS14.pin7, C2.1, C4.0, RE1.EncoderPinC, C5.1, MC14495.pin7, MC14495.pin8, MC14495.pin11, 5161AS.common_anode
  N2: J6.pin3, J6.pin4, 74LS169.pin9, 74LS169.pin16, C1.0, 74LS14.pin13, 74LS14.pin14, C2.0, R1.Pin_0, R2.Pin_0
  N3: J7.pin1, 74LS169.pin11, MC14495.pin10
  N4: J7.pin2, 74LS169.pin12, MC14495.pin9
  N5: J7.pin3, 74LS169.pin13, MC14495.pin6
  N6: J7.pin4, 74LS169.pin14, MC14495.pin5
  N7: 74LS169.pin1, 74LS14.pin10
  N8: 74LS169.pin2, 74LS14.pin8
  N9: 74LS14.pin9, C4.1, RE1.EncoderPinB, R2.Pin_1
  N10: 74LS14.pin11, RE1.EncoderPinA, C5.0, R1.Pin_1
  N11: MC14495.pin1, 5161AS.Segment_E
  N12: MC14495.pin2, 5161AS.Segment_F
  N13: MC14495.pin3, 5161AS.Segment_G
  N14: MC14495.pin4, 5161AS.Segment_DP
  N15: MC14495.pin12, 5161AS.Segment_A
  N16: MC14495.pin13, 5161AS.Segment_B
  N17: MC14495.pin14, 5161AS.Segment_C
  N18: MC14495.pin15, 5161AS.Segment_D

notes:
  0
  1
  2
  3
  +
  -
