# Fritzing sketch outregdisp_v2 (saved by Fritzing 0.9.1b)
circuit board: 9.99cm x 9.99cm
breadboards: 1

parts:
  555 = 555 Timer [package="DIP8 [THT]"]
  74LS163 = IC, DIP package, 16 pins [chip_label=IC]
  C1 = Ceramic Capacitor [capacitance=100nF package="100 mil [THT, multilayer]"]
  74LS139 = IC, DIP package, 16 pins [chip_label=IC]
  C2 = Ceramic Capacitor [capacitance=100nF package="100 mil [THT, multilayer]"]
  display-3 = female pin header, 6 pins [form="♀ (female)"]
  display-4 = female pin header, 6 pins [form="♀ (female)"]
  R2 = Resistor [tolerance=±5% resistance=220 package="1206 [SMD]"]
  R1 = Resistor [tolerance=±5% resistance=220 package="1206 [SMD]"]
  J49 = female pin header, 8 pins [form="♀ (female)"]  # not connected
  J50 = female pin header, 8 pins [form="♀ (female)"]  # not connected
  J51 = female pin header, 8 pins [form="♀ (female)"]  # not connected
  J52 = female pin header, 8 pins [form="♀ (female)"]
  IC14 = TSSOP20 [chip_label=IC package=TSSOP]
  R3 = Resistor [tolerance=±5% resistance=220 package="1206 [SMD]"]
  R4 = Resistor [tolerance=±5% resistance=220 package="1206 [SMD]"]
  R5 = Resistor [tolerance=±5% resistance=220 package="1206 [SMD]"]
  R6 = Resistor [tolerance=±5% resistance=220 package="1206 [SMD]"]
  R7 = Resistor [tolerance=±5% resistance=220 package="1206 [SMD]"]
  R8 = Resistor [tolerance=±5% resistance=220 package="1206 [SMD]"]
  R9 = Resistor [tolerance=±5% resistance=220 package="1206 [SMD]"]
  R10 = Resistor [tolerance=±5% resistance=220 package="1206 [SMD]"]
  J53 = female pin header, 8 pins [form="♀ (female)"]
  R11 = Resistor [tolerance=±5% resistance=220 package="1206 [SMD]"]
  R12 = Resistor [tolerance=±5% resistance=220 package="1206 [SMD]"]
  R13 = Resistor [tolerance=±5% resistance=220 package="1206 [SMD]"]
  R14 = Resistor [tolerance=±5% resistance=220 package="1206 [SMD]"]
  R15 = Resistor [tolerance=±5% resistance=220 package="1206 [SMD]"]
  R16 = Resistor [tolerance=±5% resistance=220 package="1206 [SMD]"]
  R17 = Resistor [tolerance=±5% resistance=220 package="1206 [SMD]"]
  R18 = Resistor [tolerance=±5% resistance=220 package="1206 [SMD]"]
  IC15 = TSSOP20 [chip_label=IC package=TSSOP]
  J54 = female pin header, 8 pins [form="♀ (female)"]
  R19 = Resistor [tolerance=±5% resistance=220 package="1206 [SMD]"]
  R20 = Resistor [tolerance=±5% resistance=220 package="1206 [SMD]"]
  R21 = Resistor [tolerance=±5% resistance=220 package="1206 [SMD]"]
  R22 = Resistor [tolerance=±5% resistance=220 package="1206 [SMD]"]
  R23 = Resistor [tolerance=±5% resistance=220 package="1206 [SMD]"]
  R24 = Resistor [tolerance=±5% resistance=220 package="1206 [SMD]"]
  R25 = Resistor [tolerance=±5% resistance=220 package="1206 [SMD]"]
  R26 = Resistor [tolerance=±5% resistance=220 package="1206 [SMD]"]
  IC16 = TSSOP20 [chip_label=IC package=TSSOP]
  J48 = female pin header, 14 pins [form="♀ (female)"]  # not connected
  J47 = female pin header, 14 pins [form="♀ (female)"]  # not connected
  R27 = Resistor [tolerance=±5% resistance=220 package="1206 [SMD]"]
  R28 = Resistor [tolerance=±5% resistance=220 package="1206 [SMD]"]
  R29 = Resistor [tolerance=±5% resistance=220 package="1206 [SMD]"]
  R30 = Resistor [tolerance=±5% resistance=220 package="1206 [SMD]"]
  R31 = Resistor [tolerance=±5% resistance=220 package="1206 [SMD]"]
  R32 = Resistor [tolerance=±5% resistance=220 package="1206 [SMD]"]
  R33 = Resistor [tolerance=±5% resistance=220 package="1206 [SMD]"]
  R34 = Resistor [tolerance=±5% resistance=220 package="1206 [SMD]"]
  IC17 = TSSOP20 [chip_label=IC package=TSSOP]
  J55 = female pin header, 8 pins [form="♀ (female)"]  # not connected
  display-5 = female pin header, 6 pins [form="♀ (female)"]
  display-6 = female pin header, 6 pins [form="♀ (female)"]
  R35 = Resistor [tolerance=±5% resistance=220 package="1206 [SMD]"]
  R36 = Resistor [tolerance=±5% resistance=220 package="1206 [SMD]"]
  R37 = Resistor [tolerance=±5% resistance=220 package="1206 [SMD]"]
  R38 = Resistor [tolerance=±5% resistance=220 package="1206 [SMD]"]
  R39 = Resistor [tolerance=±5% resistance=220 package="1206 [SMD]"]
  R40 = Resistor [tolerance=±5% resistance=220 package="1206 [SMD]"]
  R41 = Resistor [tolerance=±5% resistance=220 package="1206 [SMD]"]
  R42 = Resistor [tolerance=±5% resistance=220 package="1206 [SMD]"]
  IC18 = TSSOP20 [chip_label=IC package=TSSOP]

nets:
  N1: 555.Ground, 74LS163.pin8, C1.1, 74LS139.pin1, 74LS139.pin8, 74LS139.pin15, C2.0
  N2: 555.Trigger, 555.Threshold, C1.0, R2.Pin_0
  N3: 555.Output, 74LS163.pin2
  N4: 555.Discharge, R2.Pin_1, R1.Pin_0
  N5: 555.Vcc_Supply_Voltage, 74LS163.pin1, 74LS163.pin7, 74LS163.pin9, 74LS163.pin10, 74LS163.pin16, 74LS139.pin16, C2.1, R1.Pin_1
  N6: 74LS163.pin11, 74LS139.pin13
  N7: 74LS163.pin12, 74LS139.pin14
  N8: 74LS163.pin13, 74LS139.pin3
  N9: 74LS163.pin14, 74LS139.pin2
  N10: 74LS139.pin4, display-4.pin1, display-6.pin1
  N11: 74LS139.pin5, display-4.pin4
  N12: 74LS139.pin6, display-4.pin5, display-6.pin5
  N13: 74LS139.pin7, display-3.pin6, display-5.pin6
  N14: display-3.pin1, R30.Pin_1
  N15: display-3.pin2, R31.Pin_1
  N16: display-3.pin3, R29.Pin_1
  N17: display-3.pin4, R32.Pin_1
  N18: display-3.pin5, R27.Pin_1
  N19: display-4.pin2, R34.Pin_1
  N20: display-4.pin3, R28.Pin_1
  N21: display-4.pin6, R33.Pin_1
  N22: J52.pin1, IC14.2
  N23: J52.pin2, IC14.3
  N24: J52.pin3, IC14.4
  N25: J52.pin4, IC14.5
  N26: J52.pin5, IC14.6
  N27: J52.pin6, IC14.7
  N28: J52.pin7, IC14.8
  N29: J52.pin8, IC14.9
  N30: IC14.11, R8.Pin_0
  N31: IC14.12, R10.Pin_0
  N32: IC14.13, R9.Pin_0
  N33: IC14.14, R7.Pin_0
  N34: IC14.15, R6.Pin_0
  N35: IC14.16, R5.Pin_0
  N36: IC14.17, R4.Pin_0
  N37: IC14.18, R3.Pin_0
  N38: J53.pin1, IC15.2
  N39: J53.pin2, IC15.3
  N40: J53.pin3, IC15.4
  N41: J53.pin4, IC15.5
  N42: J53.pin5, IC15.6
  N43: J53.pin6, IC15.7
  N44: J53.pin7, IC15.8
  N45: J53.pin8, IC15.9
  N46: R11.Pin_0, IC15.12
  N47: R12.Pin_0, IC15.13
  N48: R13.Pin_0, IC15.11
  N49: R14.Pin_0, IC15.14
  N50: R15.Pin_0, IC15.15
  N51: R16.Pin_0, IC15.16
  N52: R17.Pin_0, IC15.17
  N53: R18.Pin_0, IC15.18
  N54: J54.pin1, IC16.2
  N55: J54.pin2, IC16.3
  N56: J54.pin3, IC16.4
  N57: J54.pin4, IC16.5
  N58: J54.pin5, IC16.6
  N59: J54.pin6, IC16.7
  N60: J54.pin7, IC16.8
  N61: J54.pin8, IC16.9
  N62: R19.Pin_0, IC16.12
  N63: R20.Pin_0, IC16.13
  N64: R21.Pin_0, IC16.11
  N65: R22.Pin_0, IC16.14
  N66: R23.Pin_0, IC16.15
  N67: R24.Pin_0, IC16.16
  N68: R25.Pin_0, IC16.17
  N69: R26.Pin_0, IC16.18
  N70: R27.Pin_0, IC17.12
  N71: R28.Pin_0, IC17.13
  N72: R29.Pin_0, IC17.11
  N73: R30.Pin_0, IC17.14
  N74: R31.Pin_0, IC17.15
  N75: R32.Pin_0, IC17.16
  N76: R33.Pin_0, IC17.17
  N77: R34.Pin_0, IC17.18
  N78: IC17.2, IC18.2
  N79: IC17.3, IC18.3
  N80: IC17.4, IC18.4
  N81: IC17.5, IC18.5
  N82: IC17.6, IC18.6
  N83: IC17.7, IC18.7
  N84: IC17.8, IC18.8
  N85: IC17.9, IC18.9
  N86: display-5.pin1, R38.Pin_1
  N87: display-5.pin2, R39.Pin_1
  N88: display-5.pin3, R37.Pin_1
  N89: display-5.pin4, R40.Pin_1
  N90: display-5.pin5, R35.Pin_1
  N91: display-6.pin2, R42.Pin_1
  N92: display-6.pin3, R36.Pin_1
  N93: display-6.pin6, R41.Pin_1
  N94: R35.Pin_0, IC18.12
  N95: R36.Pin_0, IC18.13
  N96: R37.Pin_0, IC18.11
  N97: R38.Pin_0, IC18.14
  N98: R39.Pin_0, IC18.15
  N99: R40.Pin_0, IC18.16
  N100: R41.Pin_0, IC18.17
  N101: R42.Pin_0, IC18.18
