# Fritzing sketch outregdisp_v2_wsop20 (saved by Fritzing 0.9.1b)
circuit board: 9.99cm x 9.99cm
breadboards: 1

parts:
  555 = 555 Timer [package="DIP8 [THT]"]
  74LS163 = IC, DIP package, 16 pins [chip_label=IC]
  C1 = Ceramic Capacitor [capacitance=100nF package="100 mil [THT, multilayer]"]
  74LS139 = IC, DIP package, 16 pins [chip_label=IC]
  C2 = Ceramic Capacitor [capacitance=100nF package="100 mil [THT, multilayer]"]
  R2 = Resistor [tolerance=±5% resistance=220 package="1206 [SMD]"]
  R1 = Resistor [tolerance=±5% resistance=220 package="1206 [SMD]"]
  C3 = Electrolytic Capacitor [capacitance=1µF package="100 mil [THT, electrolytic]"]
  J62 = female pin header, 2 pins [form="♀ (female)"]
  J63 = female pin header, 2 pins [form="♀ (female)"]
  J65 = female pin header, 14 pins [form="♀ (female)"]  # not connected
  J66 = female pin header, 14 pins [form="♀ (female)"]  # not connected
  J67 = female pin header, 5 pins [form="♀ (female)"]  # not connected
  J68 = female pin header, 8 pins [form="♀ (female)"]
  R107 = Resistor [tolerance=±5% resistance=220 package="1206 [SMD]"]
  R108 = Resistor [tolerance=±5% resistance=220 package="1206 [SMD]"]
  R109 = Resistor [tolerance=±5% resistance=220 package="1206 [SMD]"]
  R110 = Resistor [tolerance=±5% resistance=220 package="1206 [SMD]"]
  R111 = Resistor [tolerance=±5% resistance=220 package="1206 [SMD]"]
  R112 = Resistor [tolerance=±5% resistance=220 package="1206 [SMD]"]
  R113 = Resistor [tolerance=±5% resistance=220 package="1206 [SMD]"]
  R114 = Resistor [tolerance=±5% resistance=220 package="1206 [SMD]"]
  IC29 = SO20W [chip_label=IC package=SO(w)]
  J69 = female pin header, 8 pins [form="♀ (female)"]
  R115 = Resistor [tolerance=±5% resistance=220 package="1206 [SMD]"]
  R116 = Resistor [tolerance=±5% resistance=220 package="1206 [SMD]"]
  R117 = Resistor [tolerance=±5% resistance=220 package="1206 [SMD]"]
  R118 = Resistor [tolerance=±5% resistance=220 package="1206 [SMD]"]
  R119 = Resistor [tolerance=±5% resistance=220 package="1206 [SMD]"]
  R120 = Resistor [tolerance=±5% resistance=220 package="1206 [SMD]"]
  R121 = Resistor [tolerance=±5% resistance=220 package="1206 [SMD]"]
  R122 = Resistor [tolerance=±5% resistance=220 package="1206 [SMD]"]
  IC30 = SO20W [chip_label=IC package=SO(w)]
  J77 = female pin header, 8 pins [form="♀ (female)"]  # not connected
  J78 = female pin header, 8 pins [form="♀ (female)"]  # not connected
  J79 = female pin header, 8 pins [form="♀ (female)"]  # not connected
  J80 = female pin header, 8 pins [form="♀ (female)"]
  J81 = female pin header, 8 pins [form="♀ (female)"]  # not connected
  R123 = Resistor [tolerance=±5% resistance=220 package="1206 [SMD]"]
  R124 = Resistor [tolerance=±5% resistance=220 package="1206 [SMD]"]
  R125 = Resistor [tolerance=±5% resistance=220 package="1206 [SMD]"]
  R126 = Resistor [tolerance=±5% resistance=220 package="1206 [SMD]"]
  R127 = Resistor [tolerance=±5% resistance=220 package="1206 [SMD]"]
  R128 = Resistor [tolerance=±5% resistance=220 package="1206 [SMD]"]
  R129 = Resistor [tolerance=±5% resistance=220 package="1206 [SMD]"]
  R130 = Resistor [tolerance=±5% resistance=220 package="1206 [SMD]"]
  IC31 = SO20W [chip_label=IC package=SO(w)]
  J82 = female pin header, 8 pins [form="♀ (female)"]
  R131 = Resistor [tolerance=±5% resistance=220 package="1206 [SMD]"]
  R132 = Resistor [tolerance=±5% resistance=220 package="1206 [SMD]"]
  R133 = Resistor [tolerance=±5% resistance=220 package="1206 [SMD]"]
  R134 = Resistor [tolerance=±5% resistance=220 package="1206 [SMD]"]
  R135 = Resistor [tolerance=±5% resistance=220 package="1206 [SMD]"]
  R136 = Resistor [tolerance=±5% resistance=220 package="1206 [SMD]"]
  R137 = Resistor [tolerance=±5% resistance=220 package="1206 [SMD]"]
  R138 = Resistor [tolerance=±5% resistance=220 package="1206 [SMD]"]
  IC32 = SO20W [chip_label=IC package=SO(w)]
  J83 = female pin header, 14 pins [form="♀ (female)"]  # not connected
  J84 = female pin header, 14 pins [form="♀ (female)"]
  J85 = female pin header, 5 pins [form="♀ (female)"]  # not connected
  IC33 = SO20W [chip_label=IC package=SO(w)]
  R139 = Resistor [tolerance=±5% resistance=220 package="1206 [SMD]"]
  R140 = Resistor [tolerance=±5% resistance=220 package="1206 [SMD]"]
  R141 = Resistor [tolerance=±5% resistance=220 package="1206 [SMD]"]
  R142 = Resistor [tolerance=±5% resistance=220 package="1206 [SMD]"]
  R143 = Resistor [tolerance=±5% resistance=220 package="1206 [SMD]"]
  R144 = Resistor [tolerance=±5% resistance=220 package="1206 [SMD]"]
  R145 = Resistor [tolerance=±5% resistance=220 package="1206 [SMD]"]
  R146 = Resistor [tolerance=±5% resistance=220 package="1206 [SMD]"]
  display-15 = female pin header, 6 pins [form="♀ (female)"]
  display-16 = female pin header, 6 pins [form="♀ (female)"]
  IC34 = SO20W [chip_label=IC package=SO(w)]
  R147 = Resistor [tolerance=±5% resistance=220 package="1206 [SMD]"]
  R148 = Resistor [tolerance=±5% resistance=220 package="1206 [SMD]"]
  R149 = Resistor [tolerance=±5% resistance=220 package="1206 [SMD]"]
  R150 = Resistor [tolerance=±5% resistance=220 package="1206 [SMD]"]
  R151 = Resistor [tolerance=±5% resistance=220 package="1206 [SMD]"]
  R152 = Resistor [tolerance=±5% resistance=220 package="1206 [SMD]"]
  R153 = Resistor [tolerance=±5% resistance=220 package="1206 [SMD]"]
  R154 = Resistor [tolerance=±5% resistance=220 package="1206 [SMD]"]
  display-17 = female pin header, 6 pins [form="♀ (female)"]
  display-18 = female pin header, 6 pins [form="♀ (female)"]
  IC35 = SO20W [chip_label=IC package=SO(w)]
  IC36 = SO20W [chip_label=IC package=SO(w)]
  R155 = Resistor [tolerance=±5% resistance=220 package="1206 [SMD]"]
  R156 = Resistor [tolerance=±5% resistance=220 package="1206 [SMD]"]
  R157 = Resistor [tolerance=±5% resistance=220 package="1206 [SMD]"]
  R158 = Resistor [tolerance=±5% resistance=220 package="1206 [SMD]"]
  R159 = Resistor [tolerance=±5% resistance=220 package="1206 [SMD]"]
  R160 = Resistor [tolerance=±5% resistance=220 package="1206 [SMD]"]
  R161 = Resistor [tolerance=±5% resistance=220 package="1206 [SMD]"]
  R162 = Resistor [tolerance=±5% resistance=220 package="1206 [SMD]"]
  R163 = Resistor [tolerance=±5% resistance=220 package="1206 [SMD]"]
  R164 = Resistor [tolerance=±5% resistance=220 package="1206 [SMD]"]
  R165 = Resistor [tolerance=±5% resistance=220 package="1206 [SMD]"]
  R166 = Resistor [tolerance=±5% resistance=220 package="1206 [SMD]"]
  R167 = Resistor [tolerance=±5% resistance=220 package="1206 [SMD]"]
  R168 = Resistor [tolerance=±5% resistance=220 package="1206 [SMD]"]
  R169 = Resistor [tolerance=±5% resistance=220 package="1206 [SMD]"]
  R170 = Resistor [tolerance=±5% resistance=220 package="1206 [SMD]"]
  display-19 = female pin header, 6 pins [form="♀ (female)"]
  display-20 = female pin header, 6 pins [form="♀ (female)"]
  display-21 = female pin header, 6 pins [form="♀ (female)"]
  display-22 = female pin header, 6 pins [form="♀ (female)"]

nets:
  N1: 555.Ground, 74LS163.pin8, C1.1, 74LS139.pin1, 74LS139.pin8, 74LS139.pin15, C2.0
  N2: 555.Trigger, 555.Threshold, C1.0, R2.Pin_0
  N3: 555.Output, 74LS163.pin2
  N4: 555.Discharge, R2.Pin_1, R1.Pin_0
  N5: 555.Vcc_Supply_Voltage, 74LS163.pin1, 74LS163.pin7, 74LS163.pin9, 74LS163.pin10, 74LS163.pin16, 74LS139.pin16, C2.1, R1.Pin_1
  N6: 74LS163.pin11, 74LS139.pin13
  N7: 74LS163.pin12, 74LS139.pin14
  N8: 74LS163.pin13, 74LS139.pin3
  N9: 74LS163.pin14, 74LS139.pin2
  N10: 74LS139.pin9, IC32.19, IC33.19
  N11: 74LS139.pin10, IC31.19, IC34.19
  N12: 74LS139.pin11, IC30.19, IC35.19
  N13: 74LS139.pin12, IC29.19, IC36.19
  N14: C3.-, J62.pin1, J63.pin1, IC29.10, IC30.10, IC31.10, IC32.10, J84.pin14
  N15: C3.+, J62.pin2, J63.pin2, IC29.1, IC29.20, IC30.1, IC30.20, IC31.1, IC31.20, IC32.1, IC32.20
  N16: J68.pin1, IC29.2
  N17: J68.pin2, IC29.3
  N18: J68.pin3, IC29.4
  N19: J68.pin4, IC29.5
  N20: J68.pin5, IC29.6
  N21: J68.pin6, IC29.7
  N22: J68.pin7, IC29.8
  N23: J68.pin8, IC29.9
  N24: R107.Pin_0, IC29.12
  N25: R107.Pin_1, R115.Pin_1, R123.Pin_1, R131.Pin_1, J84.pin9
  N26: R108.Pin_0, IC29.13
  N27: R108.Pin_1, R116.Pin_1, R124.Pin_1, R132.Pin_1, J84.pin8
  N28: R109.Pin_0, IC29.11
  N29: R109.Pin_1, R117.Pin_1, R125.Pin_1, R133.Pin_1, J84.pin10
  N30: R110.Pin_0, IC29.14
  N31: R110.Pin_1, R118.Pin_1, R126.Pin_1, R134.Pin_1, J84.pin7
  N32: R111.Pin_0, IC29.15
  N33: R111.Pin_1, R119.Pin_1, R127.Pin_1, R135.Pin_1, J84.pin6
  N34: R112.Pin_0, IC29.16
  N35: R112.Pin_1, R120.Pin_1, R128.Pin_1, R136.Pin_1, J84.pin5
  N36: R113.Pin_0, IC29.17
  N37: R113.Pin_1, R121.Pin_1, R129.Pin_1, R137.Pin_1, J84.pin4
  N38: R114.Pin_0, IC29.18
  N39: R114.Pin_1, R122.Pin_1, R130.Pin_1, R138.Pin_1, J84.pin3
  N40: J69.pin1, IC30.2
  N41: J69.pin2, IC30.3
  N42: J69.pin3, IC30.4
  N43: J69.pin4, IC30.5
  N44: J69.pin5, IC30.6
  N45: J69.pin6, IC30.7
  N46: J69.pin7, IC30.8
  N47: J69.pin8, IC30.9
  N48: R115.Pin_0, IC30.12
  N49: R116.Pin_0, IC30.13
  N50: R117.Pin_0, IC30.11
  N51: R118.Pin_0, IC30.14
  N52: R119.Pin_0, IC30.15
  N53: R120.Pin_0, IC30.16
  N54: R121.Pin_0, IC30.17
  N55: R122.Pin_0, IC30.18
  N56: J80.pin1, IC31.2
  N57: J80.pin2, IC31.3
  N58: J80.pin3, IC31.4
  N59: J80.pin4, IC31.5
  N60: J80.pin5, IC31.6
  N61: J80.pin6, IC31.7
  N62: J80.pin7, IC31.8
  N63: J80.pin8, IC31.9
  N64: R123.Pin_0, IC31.12
  N65: R124.Pin_0, IC31.13
  N66: R125.Pin_0, IC31.11
  N67: R126.Pin_0, IC31.14
  N68: R127.Pin_0, IC31.15
  N69: R128.Pin_0, IC31.16
  N70: R129.Pin_0, IC31.17
  N71: R130.Pin_0, IC31.18
  N72: J82.pin2, IC32.3
  N73: J82.pin3, IC32.4
  N74: J82.pin4, IC32.5
  N75: J82.pin5, IC32.6
  N76: J82.pin6, IC32.7
  N77: J82.pin7, IC32.8
  N78: J82.pin8, IC32.9
  N79: R131.Pin_0, IC32.12
  N80: R132.Pin_0, IC32.13
  N81: R133.Pin_0, IC32.11
  N82: R134.Pin_0, IC32.14
  N83: R135.Pin_0, IC32.15
  N84: R136.Pin_0, IC32.16
  N85: R137.Pin_0, IC32.17
  N86: R138.Pin_0, IC32.18
  N87: IC33.1, IC33.10, IC34.1, IC34.10, IC35.1, IC35.10, IC36.1, IC36.10
  N88: IC33.2, R139.Pin_1
  N89: IC33.3, R140.Pin_1
  N90: IC33.4, R143.Pin_0
  N91: IC33.5, R142.Pin_1
  N92: IC33.6, R146.Pin_1
  N93: IC33.7, R141.Pin_1
  N94: IC33.8, R144.Pin_1
  N95: IC33.9, R145.Pin_1
  N96: IC33.11, IC34.11, IC35.11, IC36.11
  N97: IC33.12, IC34.12, IC35.12, IC36.12
  N98: IC33.13, IC34.13, IC35.13, IC36.13
  N99: IC33.14, IC34.14, IC35.14, IC36.14
  N100: IC33.15, IC34.15, IC35.15, IC36.15
  N101: IC33.16, IC34.16, IC35.16, IC36.16
  N102: IC33.17, IC34.17, IC35.17, IC36.17
  N103: IC33.18, IC34.18, IC35.18, IC36.18
  N104: IC33.20, IC34.20, IC35.20, IC36.20
  N105: R139.Pin_0, display-16.pin2
  N106: R140.Pin_0, display-16.pin6
  N107: R141.Pin_0, display-16.pin3
  N108: R142.Pin_0, display-15.pin2
  N109: R143.Pin_1, display-15.pin4
  N110: R144.Pin_0, display-15.pin5
  N111: R145.Pin_0, display-15.pin3
  N112: R146.Pin_0, display-15.pin1
  N113: display-15.pin6, display-17.pin6, display-19.pin6, display-20.pin6
  N114: display-16.pin1, display-18.pin1, display-21.pin1, display-22.pin1
  N115: display-16.pin4, display-18.pin4, display-21.pin4, display-22.pin4
  N116: display-16.pin5, display-18.pin5, display-21.pin5, display-22.pin5
  N117: IC34.2, R147.Pin_1
  N118: IC34.3, R148.Pin_1
  N119: IC34.4, R151.Pin_0
  N120: IC34.5, R150.Pin_1
  N121: IC34.6, R154.Pin_1
  N122: IC34.7, R149.Pin_1
  N123: IC34.8, R152.Pin_1
  N124: IC34.9, R153.Pin_1
  N125: R147.Pin_0, display-18.pin2
  N126: R148.Pin_0, display-18.pin6
  N127: R149.Pin_0, display-18.pin3
  N128: R150.Pin_0, display-17.pin2
  N129: R151.Pin_1, display-17.pin4
  N130: R152.Pin_0, display-17.pin5
  N131: R153.Pin_0, display-17.pin3
  N132: R154.Pin_0, display-17.pin1
  N133: IC35.2, R156.Pin_1
  N134: IC35.3, R158.Pin_1
  N135: IC35.4, R163.Pin_0
  N136: IC35.5, R162.Pin_1
  N137: IC35.6, R170.Pin_1
  N138: IC35.7, R160.Pin_1
  N139: IC35.8, R165.Pin_1
  N140: IC35.9, R168.Pin_1
  N141: IC36.2, R155.Pin_1
  N142: IC36.3, R157.Pin_1
  N143: IC36.4, R164.Pin_0
  N144: IC36.5, R161.Pin_1
  N145: IC36.6, R169.Pin_1
  N146: IC36.7, R159.Pin_1
  N147: IC36.8, R166.Pin_1
  N148: IC36.9, R167.Pin_1
  N149: R155.Pin_0, display-21.pin2
  N150: R156.Pin_0, display-22.pin2
  N151: R157.Pin_0, display-21.pin6
  N152: R158.Pin_0, display-22.pin6
  N153: R159.Pin_0, display-21.pin3
  N154: R160.Pin_0, display-22.pin3
  N155: R161.Pin_0, display-19.pin2
  N156: R162.Pin_0, display-20.pin2
  N157: R163.Pin_1, display-20.pin4
  N158: R164.Pin_1, display-19.pin4
  N159: R165.Pin_0, display-20.pin5
  N160: R166.Pin_0, display-19.pin5
  N161: R167.Pin_0, display-19.pin3
  N162: R168.Pin_0, display-20.pin3
  N163: R169.Pin_0, display-19.pin1
  N164: R170.Pin_0, display-20.pin1

notes:
  OUTPUT REGISTERS
  Marius Krabset 2019
  -
  +
